// Logisim project cpu.circ as structural Verilog: 1 circuit, main circuit main
module main (
  input  [31:0] INSTRUCTION,
  input  CLOCK,
  output [31:0] FETCH_ADDRESS,
  output [31:0] s0_Value,
  output [31:0] s1_Value,
  output [31:0] s2_Value,
  output [31:0] ra_Value,
  output [31:0] sp_Value
);

  wire ALUSrc, eql, ExtOp, jal, lui, main_2_signed_overflow, main_3_p1, MemToReg, MemWr, RegDst, RegWr, shift;
  wire [1:0] nPCsel;
  wire [3:0] ALUCtr;
  wire [4:0] multiplexer_1_out, multiplexer_2_out;
  wire [31:0] adder_2_out, bit_extender_2_out, immed, main_2_result, main_3_p6, multiplexer_3_out,
       multiplexer_4_out, multiplexer_5_out, multiplexer_6_out, multiplexer_7_out, multiplexer_8_out, PC_4,
       R_rs, rt, shifter_1_out, shifter_2_out, shifter_3_out, WrtData;

  Adder #(.width(32)) adder_1 (.a(INSTRUCTION), .b(32'h4), .out(PC_4));  // open: cin, cout
  Multiplexer #(.width(5), .enable("false")) multiplexer_1 (
    .in0(INSTRUCTION[20:16]), .in1(INSTRUCTION[15:11]), .out(multiplexer_1_out), .sel(RegDst));
  assign immed = {{16{ExtOp}}, INSTRUCTION[15:0]};  // Bit_Extender bit_extender_1
  Multiplexer #(.width(5), .enable("false")) multiplexer_2 (
    .in0(multiplexer_1_out), .in1({5{1'b1}}), .out(multiplexer_2_out), .sel(jal));
  Shifter #(.width(32)) shifter_1 (.in(immed), .\dist (5'b00010), .out(shifter_1_out));
  Shifter #(.width(32)) shifter_2 (.in(INSTRUCTION), .\dist (5'b00010), .out(shifter_2_out));
  Adder #(.width(32)) adder_2 (.a(PC_4), .b(shifter_1_out), .out(adder_2_out));  // open: cin, cout
  regfile_main main_1 (
    .Read_Register_1(INSTRUCTION[25:21]), .Read_Register_2(INSTRUCTION[20:16]),
    .Write_Register(multiplexer_2_out), .Write_Data(WrtData), .Write_Enable(RegWr), .Clock(CLOCK),
    .Read_Data_1(R_rs), .Read_Data_2(rt), .s0_Value(s0_Value), .s1_Value(s1_Value), .s2_Value(s2_Value),
    .ra_Value(ra_Value), .sp_Value(sp_Value));
  Multiplexer #(.width(32), .enable("false")) multiplexer_3 (
    .in0(PC_4), .in1(adder_2_out), .out(multiplexer_3_out), .sel(eql));
  Multiplexer #(.width(32), .enable("false")) multiplexer_4 (
    .in0(rt), .in1(immed), .out(multiplexer_4_out), .sel(ALUSrc));
  Multiplexer #(.select(2), .width(32), .enable("false")) multiplexer_5 (
    .in0(PC_4), .in1(multiplexer_3_out), .in2({PC_4[31:28], shifter_2_out[27:0]}), .in3(R_rs),
    .out(multiplexer_5_out), .sel(nPCsel));
  Register #(.width(32)) PC (.D(multiplexer_5_out), .Q(FETCH_ADDRESS), .clk(CLOCK));  // open: en, clr
  assign bit_extender_2_out = {{27{1'b0}}, INSTRUCTION[10:6]};  // Bit_Extender bit_extender_2
  Multiplexer #(.width(32), .enable("false")) multiplexer_6 (
    .in0(R_rs), .in1(bit_extender_2_out), .out(multiplexer_6_out), .sel(shift));
  LED led_1 (.in(main_2_signed_overflow));
  alu_main main_2 (
    .Switch(ALUCtr), .X(multiplexer_6_out), .Equal(eql), .Result(main_2_result),
    .Signed_Overflow(main_2_signed_overflow), .Y(multiplexer_4_out));
  Shifter #(.width(32)) shifter_3 (.in(immed), .\dist (5'b10000), .out(shifter_3_out));
  Multiplexer #(.width(32), .enable("false")) multiplexer_7 (
    .in0(main_2_result), .in1(shifter_3_out), .out(multiplexer_7_out), .sel(lui));
  // mem_main main_3: pin names not known; wires that end beside it: main_3_p1, multiplexer_7_out, rt, MemWr, CLOCK, main_3_p6
  Multiplexer #(.width(32), .enable("false")) multiplexer_8 (
    .in0(multiplexer_7_out), .in1(main_3_p6), .out(multiplexer_8_out), .sel(MemToReg));
  Multiplexer #(.width(32), .enable("false")) multiplexer_9 (
    .in0(multiplexer_8_out), .in1(PC_4), .out(WrtData), .sel(jal));

  // Other names for the same wires on the sheet: clk = CLOCK; fetch_addr[31:0] = FETCH_ADDRESS;
  //   funct[5:0] = INSTRUCTION[5:0]; shamt[4:0] = INSTRUCTION[10:6]; opcode[5:0] = INSTRUCTION[31:26];
  //   ra[31:0] = ra_Value; s0[31:0] = s0_Value; s1[31:0] = s1_Value; s2[31:0] = s2_Value; sp[31:0] = sp_Value

  // Notes on the sheet:
  //   Output
  //   These are outputs/inputs from run.circ
  //   Inputs
  //   These are DEBUG/TEST outputs from your circuit.
endmodule
